// Logisim project cr8.circ as structural Verilog: 6 circuits, main circuit main
module main (
);

  reg8 reg8_1 ();  // open: RE, CLK, D0, D1, D2, D3, D4, D5, D6, D7, Q0, Q1, Q2, Q3, Q4, Q5, Q6, Q7
endmodule

module dflop (
  input  D,
  input  clk,
  output Q1,
  output Q2
);

  wire and_1_out, and_2_out, not_1_out;

  not not_1 (not_1_out, D);
  and and_1 (and_1_out, not_1_out, clk);
  and and_2 (and_2_out, clk, D);
  nor nor_1 (Q1, and_1_out, Q2);
  nor nor_2 (Q2, Q1, and_2_out);

  // Notes on the sheet:
  //   clk: pull=up
endmodule

module reg1 (
  input  RE,
  input  D,
  input  clk,
  output Q
);

  wire and_1_out, and_2_out, not_1_out, or_1_out;

  not not_1 (not_1_out, RE);
  and and_1 (and_1_out, Q, not_1_out);
  and and_2 (and_2_out, RE, D);
  or or_1 (or_1_out, and_1_out, and_2_out);
  dflop dflop_1 (.D(or_1_out), .clk(clk), .Q1(Q));  // open: Q2
endmodule

module reg8 (
  input  RE,
  input  CLK,
  input  D0,
  input  D1,
  input  D2,
  input  D3,
  input  D4,
  input  D5,
  input  D6,
  input  D7,
  output Q0,
  output Q1,
  output Q2,
  output Q3,
  output Q4,
  output Q5,
  output Q6,
  output Q7
);

  reg1 reg1_1 (.RE(RE), .D(D0), .clk(CLK), .Q(Q0));
  reg1 reg1_2 (.RE(RE), .D(D1), .clk(CLK), .Q(Q1));
  reg1 reg1_3 (.RE(RE), .D(D2), .clk(CLK), .Q(Q2));
  reg1 reg1_4 (.RE(RE), .D(D3), .clk(CLK), .Q(Q3));
  reg1 reg1_5 (.RE(RE), .D(D4), .clk(CLK), .Q(Q4));
  reg1 reg1_6 (.RE(RE), .D(D5), .clk(CLK), .Q(Q5));
  reg1 reg1_7 (.RE(RE), .D(D6), .clk(CLK), .Q(Q6));
  reg1 reg1_8 (.RE(RE), .D(D7), .clk(CLK), .Q(Q7));
endmodule

module reg1ic (
  input  RE,
  input  D,
  input  CLK,
  output Q
);

  wire n7404_1_pin1, n7404_1_pin2, n7404_1_pin9, n7408_1_pin1, n7408_1_pin3, n7408_1_pin5, n7408_1_pin6,
       n7408_1_pin8, n7408_1_pin9, n7408_1_pin11;

  _7408 u_7408_1 (
    .pin1(n7408_1_pin1), .pin2(CLK), .pin3(n7408_1_pin3), .pin4(CLK), .pin5(n7408_1_pin5),
    .pin6(n7408_1_pin6), .pin13(D), .pin12(RE), .pin11(n7408_1_pin11), .pin10(Q), .pin9(n7408_1_pin9),
    .pin8(n7408_1_pin8));
  _7404 u_7404_1 (
    .pin1(n7404_1_pin1), .pin2(n7404_1_pin2), .pin13(RE), .pin12(n7408_1_pin9), .pin11(n7408_1_pin5),
    .pin10(n7408_1_pin1), .pin9(n7404_1_pin9), .pin8(Q));  // open: pin3, pin4, pin5, pin6
  _7432 u_7432_1 (
    .pin1(n7408_1_pin3), .pin2(n7404_1_pin2), .pin3(n7404_1_pin9), .pin4(n7408_1_pin6), .pin5(Q),
    .pin6(n7404_1_pin1), .pin13(n7408_1_pin11), .pin12(n7408_1_pin8), .pin11(n7408_1_pin5));  // open: pin10, pin9, pin8
endmodule

module reg8ic (
  input  RE,
  input  CLK,
  input  D0,
  input  D1,
  input  D2,
  input  D3,
  input  D4,
  input  D5,
  input  D6,
  input  D7,
  output Q0,
  output Q1,
  output Q2,
  output Q3,
  output Q4,
  output Q5,
  output Q6,
  output Q7
);

  reg1ic reg1ic_1 (.RE(RE), .D(D0), .CLK(CLK), .Q(Q0));
  reg1ic reg1ic_2 (.RE(RE), .D(D1), .CLK(CLK), .Q(Q1));
  reg1ic reg1ic_3 (.RE(RE), .D(D2), .CLK(CLK), .Q(Q2));
  reg1ic reg1ic_4 (.RE(RE), .D(D3), .CLK(CLK), .Q(Q3));
  reg1ic reg1ic_5 (.RE(RE), .D(D4), .CLK(CLK), .Q(Q4));
  reg1ic reg1ic_6 (.RE(RE), .D(D5), .CLK(CLK), .Q(Q5));
  reg1ic reg1ic_7 (.RE(RE), .D(D6), .CLK(CLK), .Q(Q6));
  reg1ic reg1ic_8 (.RE(RE), .D(D7), .CLK(CLK), .Q(Q7));
endmodule
